// Logisim project ALU_8_bit.circ as structural Verilog: 10 circuits, main circuit ALU
module ALU (
  input  Clock,
  input  CF_In,
  input  Reset,
  input  [3:0] Code,
  input  OE,
  input  [7:0] Data_In,
  input  FR,
  input  A_B,
  input  Reg_i_o,
  input  Reg_EN,
  output [7:0] Q,
  output [3:0] Flags,
  output [7:0] Reg_OE
);

  wire and_1_out, and_2_out, and_3_out, and_4_out, decoder_1_out0, decoder_1_out1, math_1_carryout,
       nor_1_out, not_1_out, not_2_out, shift_1_carry_o, xor_1_out;
  wire [1:0] pull_resistor_1_node;
  wire [3:0] not_3_out;
  wire [7:0] A_q, B_q, logic_1_c, math_1_c, multiplexer_1_out, multiplexer_2_out, multiplexer_3_out,
       shift_1_q;

  Decoder decoder_1 (.out0(decoder_1_out0), .out1(decoder_1_out1), .sel(A_B), .en(and_1_out));
  and and_1 (and_1_out, Reg_EN, ~Reg_i_o);  // AND_Gate
  and and_2 (and_2_out, Reg_EN, Reg_i_o);
  Register A (.D(Data_In), .en(decoder_1_out0), .clk(Clock), .Q(A_q), .clr(Reset));
  Register B (.D(Data_In), .en(decoder_1_out1), .clk(Clock), .Q(B_q), .clr(Reset));
  Multiplexer #(.enable("true"), .width(8)) multiplexer_1 (
    .in0(A_q), .in1(B_q), .out(multiplexer_1_out), .sel(A_B), .en(and_2_out));
  assign Reg_OE = and_2_out ? multiplexer_1_out : 8'bz;  // Controlled_Buffer controlled_buffer_1
  // Probe on B_q
  D_Flip_Flop d_ff_1 (.clk(Clock), .D(CF_In));  // open: Q, Qn, preset, reset
  // Probe on A_q
  Multiplexer #(.width(8)) multiplexer_2 (.in0(B_q), .in1(8'h1), .out(multiplexer_2_out), .sel(Code[3]));
  and and_3 (and_3_out, Code[2], Code[1], Code[0]);
  xor xor_1 (xor_1_out, and_3_out, Code[0]);
  not not_1 (not_1_out, and_3_out);
  Pull_Resistor pull_resistor_1 (.node(pull_resistor_1_node));
  assign pull_resistor_1_node = not_1_out ? Code[3:2] : 2'bz;  // Controlled_Buffer controlled_buffer_2
  Math math_1 (
    .Carry(xor_1_out), .Negate(Code[1]), .B(A_q), .A(multiplexer_2_out), .C(math_1_c),
    .CarryOut(math_1_carryout));
  Logic logic_1 (.data1(Code[0]), .data2(Code[1]), .A(A_q), .B(multiplexer_2_out), .C(logic_1_c));
  Shift shift_1 (
    .carry(Code[1]), .A(A_q), .B(multiplexer_2_out), .mode(Code[1:0]), .carry_o(shift_1_carry_o),
    .q(shift_1_q));
  and and_4 (and_4_out, not_1_out, OE);
  assign Q = and_4_out ? multiplexer_3_out : 8'bz;  // Controlled_Buffer controlled_buffer_3
  Multiplexer #(.select(2), .width(8)) multiplexer_3 (
    .in0(math_1_c), .in1(logic_1_c), .in2(shift_1_q), .in3(math_1_c), .out(multiplexer_3_out),
    .sel(pull_resistor_1_node));
  nor nor_1 (nor_1_out, multiplexer_3_out[1], multiplexer_3_out[2], multiplexer_3_out[3], multiplexer_3_out[4], multiplexer_3_out[5], multiplexer_3_out[6], multiplexer_3_out[7]);
  // Probe on Q
  Multiplexer #(.select(2)) multiplexer_4 (
    .in0(math_1_carryout), .in1(1'b0), .in2(shift_1_carry_o), .in3(math_1_carryout), .out(not_3_out[3]),
    .sel(pull_resistor_1_node));
  not not_2 (not_2_out, multiplexer_3_out[0]);
  not not_3 (not_3_out[0], multiplexer_3_out[0]);
  assign Flags = FR ? not_3_out : 4'bz;  // Controlled_Buffer controlled_buffer_4
  and and_5 (not_3_out[2], not_2_out, nor_1_out);
  and and_6 (not_3_out[1], nor_1_out, multiplexer_3_out[0]);

  // Notes on the sheet:
  //   00xx math 01xx logic 10xx rotate 11xx inc/dec
  //   0000 add 0001 adc 0010 sub 0011 sbb 0100 ana 0101 xra 0110 ora 0111 cmp 1000 rlc 1001 rrc 1010 ral 1011 rar 1100 INC 1110 DEC
  //   Carry
  //   Zero
  //   One
  //   Even
endmodule

module full_ADD_SUB_one_bit (
  input  A,
  input  B,
  input  C,
  input  Negate,
  output O,
  output Carry
);

  wire and_1_out, and_2_out, and_3_out, xor_1_out, xor_2_out;

  xor xor_1 (xor_1_out, Negate, A);
  xor xor_2 (xor_2_out, A, B);
  xor xor_3 (O, xor_2_out, C);
  and and_1 (and_1_out, B, C);
  and and_2 (and_2_out, C, xor_1_out);
  and and_3 (and_3_out, B, xor_1_out);
  or or_1 (Carry, and_1_out, and_2_out, and_3_out);

  // Notes on the sheet:
  //   N = 0 : A+B+C
  //   N = 1 : A-B-C
endmodule

module Math (
  input  Carry,
  input  Negate,
  input  [7:0] B,
  input  [7:0] A,
  output [7:0] C,
  output CarryOut
);

  wire full_add_sub_one_bit_1_carry, full_add_sub_one_bit_2_carry, full_add_sub_one_bit_3_carry,
       full_add_sub_one_bit_4_carry, full_add_sub_one_bit_5_carry, full_add_sub_one_bit_6_carry,
       full_add_sub_one_bit_7_carry;

  full_ADD_SUB_one_bit full_add_sub_one_bit_1 (
    .A(B[0]), .B(A[0]), .C(Carry), .Negate(Negate), .O(C[0]), .Carry(full_add_sub_one_bit_1_carry));
  full_ADD_SUB_one_bit full_add_sub_one_bit_2 (
    .A(B[1]), .B(A[1]), .C(full_add_sub_one_bit_1_carry), .Negate(Negate), .O(C[1]),
    .Carry(full_add_sub_one_bit_2_carry));
  full_ADD_SUB_one_bit full_add_sub_one_bit_3 (
    .A(B[2]), .B(A[2]), .C(full_add_sub_one_bit_2_carry), .Negate(Negate), .O(C[2]),
    .Carry(full_add_sub_one_bit_3_carry));
  full_ADD_SUB_one_bit full_add_sub_one_bit_4 (
    .A(B[3]), .B(A[3]), .C(full_add_sub_one_bit_3_carry), .Negate(Negate), .O(C[3]),
    .Carry(full_add_sub_one_bit_4_carry));
  full_ADD_SUB_one_bit full_add_sub_one_bit_5 (
    .A(B[4]), .B(A[4]), .C(full_add_sub_one_bit_4_carry), .Negate(Negate), .O(C[4]),
    .Carry(full_add_sub_one_bit_5_carry));
  full_ADD_SUB_one_bit full_add_sub_one_bit_6 (
    .A(B[5]), .B(A[5]), .C(full_add_sub_one_bit_5_carry), .Negate(Negate), .O(C[5]),
    .Carry(full_add_sub_one_bit_6_carry));
  full_ADD_SUB_one_bit full_add_sub_one_bit_7 (
    .A(B[6]), .B(A[6]), .C(full_add_sub_one_bit_6_carry), .Negate(Negate), .O(C[6]),
    .Carry(full_add_sub_one_bit_7_carry));
  full_ADD_SUB_one_bit full_add_sub_one_bit_8 (
    .A(B[7]), .B(A[7]), .C(full_add_sub_one_bit_7_carry), .Negate(Negate), .O(C[7]), .Carry(CarryOut));
endmodule

module Rotate (
  input  left_right,
  input  carry,
  input  [7:0] A,
  output [7:0] C,
  output carryOut
);

  Multiplexer #(.width(8)) multiplexer_1 (.in0({A[6:0], carry}), .in1({carry, A[7:1]}), .out(C), .sel(left_right));
  Multiplexer multiplexer_2 (.in0(A[7]), .in1(A[0]), .out(carryOut), .sel(left_right));

  // Notes on the sheet:
  //   data1 = left or right // data2 = with or without carry
endmodule

module Logic (
  input  data1,
  input  data2,
  input  [7:0] A,
  input  [7:0] B,
  output [7:0] C
);

  wire [7:0] and_1_out, or_1_out, xor_1_out;

  assign and_1_out = A & B;  // AND_Gate and_1, 8 bits wide
  assign xor_1_out = A ^ B;  // XOR_Gate xor_1, 8 bits wide
  assign or_1_out = A | B;  // OR_Gate or_1, 8 bits wide
  Multiplexer #(.select(2), .width(8)) multiplexer_1 (
    .in0(and_1_out), .in1(xor_1_out), .in2(or_1_out), .out(C), .sel({data2, data1}));  // open: in3
endmodule

module Registers (
  input  Clock,
  input  Reset,
  input  [7:0] D_In,
  input  Red_Enable,
  input  Write_Enable,
  input  [2:0] Addr_reg_Out,
  input  [2:0] Addr_reg_In,
  input  Arith_Ope,
  input  Addr_Select,
  output [7:0] D_Out,
  output [15:0] Addr_Out
);

  wire decoder_1_out0, decoder_1_out1, decoder_1_out2, decoder_1_out3, decoder_1_out4, decoder_1_out5,
       decoder_1_out6, xor_1_out, xor_2_out;
  wire [2:0] pull_resistor_1_node, pull_resistor_2_node;
  wire [7:0] A_q, B_q, C_q, D_q, E_q, H_q, L_q, multiplexer_1_out;

  Decoder #(.select(3)) decoder_1 (
    .out0(decoder_1_out0), .out1(decoder_1_out1), .out2(decoder_1_out2), .out3(decoder_1_out3),
    .out4(decoder_1_out4), .out5(decoder_1_out5), .out6(decoder_1_out6), .sel(pull_resistor_1_node),
    .en(Write_Enable));  // open: out7
  Pull_Resistor pull_resistor_1 (.node(pull_resistor_1_node));
  assign pull_resistor_1_node = xor_1_out ? Addr_reg_In : 3'bz;  // Controlled_Buffer controlled_buffer_1
  xor xor_1 (xor_1_out, Write_Enable, Arith_Ope);
  Register A (.D(D_In), .en(decoder_1_out0), .Q(A_q), .clk(Clock), .clr(Reset));
  Register B (.D(D_In), .en(decoder_1_out1), .Q(B_q), .clk(Clock), .clr(Reset));
  Register C (.D(D_In), .en(decoder_1_out2), .Q(C_q), .clk(Clock), .clr(Reset));
  Register D (.D(D_In), .en(decoder_1_out3), .Q(D_q), .clk(Clock), .clr(Reset));
  Register E (.D(D_In), .en(decoder_1_out4), .Q(E_q), .clk(Clock), .clr(Reset));
  Register H (.D(D_In), .en(decoder_1_out5), .Q(H_q), .clk(Clock), .clr(Reset));
  Register L (.D(D_In), .en(decoder_1_out6), .Q(L_q), .clk(Clock), .clr(Reset));
  assign Addr_Out = Addr_Select ? {H_q, L_q} : 16'bz;  // Controlled_Buffer controlled_buffer_2
  Multiplexer #(.enable("true"), .select(3), .width(8)) multiplexer_1 (
    .in0(A_q), .in1(B_q), .in2(C_q), .in3(D_q), .in4(E_q), .in5(H_q), .in6(L_q), .out(multiplexer_1_out),
    .sel(pull_resistor_2_node), .en(Red_Enable));  // open: in7
  Pull_Resistor pull_resistor_2 (.node(pull_resistor_2_node));
  assign pull_resistor_2_node = xor_2_out ? Addr_reg_Out : 3'bz;  // Controlled_Buffer controlled_buffer_3
  xor xor_2 (xor_2_out, Red_Enable, Arith_Ope);
  assign D_Out = Red_Enable ? multiplexer_1_out : 8'bz;  // Controlled_Buffer controlled_buffer_4
endmodule

module Main (
  input  Reset
);

  wire clock_1_out;
  wire [7:0] alu_1_q;

  ALU alu_1 (
    .Clock(clock_1_out), .Reset(Reset), .Data_In(alu_1_q), .Q(alu_1_q), .Reg_OE(alu_1_q));  // open: CF_In, Code, OE, FR, A_B, Reg_i_o, Reg_EN, Flags
  Clock clock_1 (.out(clock_1_out));
  Registers registers_1 (
    .Reset(Reset), .D_In(alu_1_q), .D_Out(alu_1_q));  // open: Clock, Red_Enable, Write_Enable, Addr_reg_Out, Addr_reg_In, Arith_Ope, Addr_Select, Addr_Out
  AS_PC as_pc_1 (.Reset(Reset), .Clock(clock_1_out));  // open: Pop, Push, Data_In, Set, L_H, Enable, Addr_Out
  Data_Stack data_stack_1 (
    .Reset(Reset), .Clock(clock_1_out), .Data_In(alu_1_q), .Data_Out(alu_1_q));  // open: Pop, Push
endmodule

module Data_Stack (
  input  Pop,
  input  Push,
  input  Reset,
  input  Clock,
  input  [7:0] Data_In,
  output [7:0] Data_Out
);

  wire and_1_out, not_1_out, xnor_1_out, xor_1_out;
  wire [7:0] counter_1_q, multiplexer_1_out, pull_resistor_1_node, ram_1_dout;

  xor xor_1 (xor_1_out, Pop, Push);
  Counter counter_1 (.count(xor_1_out), .Q(counter_1_q), .up(Push), .clk(Clock), .clr(Reset));  // open: load, D, carry
  xnor xnor_1 (xnor_1_out, Push, Clock);
  Pull_Resistor pull_resistor_1 (.node(pull_resistor_1_node));
  RAM #(.clearpin("true"), .readbehav("war")) ram_1 (
    .addr(counter_1_q), .we(xor_1_out), .oe(not_1_out), .clk(xnor_1_out), .din(multiplexer_1_out),
    .dout(ram_1_dout), .clr(Reset));
  not not_1 (not_1_out, Push);
  Multiplexer #(.width(8)) multiplexer_1 (
    .in0(pull_resistor_1_node), .in1(Data_In), .out(multiplexer_1_out), .sel(Push));
  and and_1 (and_1_out, xor_1_out, not_1_out);
  assign Data_Out = and_1_out ? ram_1_dout : 8'bz;  // Controlled_Buffer controlled_buffer_1
endmodule

module Shift (
  input  carry,
  input  [7:0] A,
  input  [7:0] B,
  input  [1:0] mode,
  output carry_o,
  output [7:0] q
);

  wire [7:0] shifter_1_out, shifter_2_out, shifter_3_out, shifter_4_out;

  Shifter #(.shift("rl")) shifter_1 (.in(A), .\dist (B[2:0]), .out(shifter_1_out));
  Multiplexer #(.select(2)) multiplexer_1 (.in0(A[7]), .in1(A[0]), .in2(A[7]), .in3(A[0]), .out(carry_o), .sel(mode));
  Shifter #(.shift("rr")) shifter_2 (.in(A), .\dist (B[2:0]), .out(shifter_2_out));
  Shifter shifter_3 (.in(A), .\dist (B[2:0]), .out(shifter_3_out));
  Shifter #(.shift("lr")) shifter_4 (.in(A), .\dist (B[2:0]), .out(shifter_4_out));
  Multiplexer #(.select(2), .width(8)) multiplexer_2 (
    .in0(shifter_1_out), .in1(shifter_2_out), .in2({shifter_3_out[7:1], carry}),
    .in3({carry, shifter_4_out[6:0]}), .out(q), .sel(mode));
endmodule

module AS_PC (
  input  Reset,
  input  Clock,
  input  Pop,
  input  Push,
  input  [7:0] Data_In,
  input  Set,
  input  L_H,
  input  Enable,
  output [15:0] Addr_Out
);

  wire decoder_1_out0, decoder_1_out1, multiplexer_1_out, not_1_out, not_2_out, or_1_out, or_2_out;
  wire [7:0] counter_1_q, H_q, L_q;
  wire [15:0] counter_2_q, multiplexer_2_out, ram_1_dout;

  Decoder decoder_1 (.out0(decoder_1_out0), .out1(decoder_1_out1), .sel(L_H), .en(Set));
  or or_1 (or_1_out, Pop, Push);
  Register L (.D(Data_In), .en(decoder_1_out0), .Q(L_q), .clk(Clock), .clr(Reset));
  Register H (.D(Data_In), .en(decoder_1_out1), .Q(H_q), .clk(Clock), .clr(Reset));
  Counter counter_1 (
    .count(or_1_out), .Q(counter_1_q), .up(Push), .clk(multiplexer_1_out), .clr(Reset));  // open: load, D, carry
  Multiplexer multiplexer_1 (.in0(Clock), .in1(not_1_out), .out(multiplexer_1_out), .sel(Pop));
  not not_1 (not_1_out, Clock);
  not not_2 (not_2_out, Pop);
  Multiplexer #(.width(16)) multiplexer_2 (
    .in0(ram_1_dout), .in1({H_q, L_q}), .out(multiplexer_2_out), .sel(not_2_out));
  RAM #(.clearpin("true"), .dataWidth(16)) ram_1 (
    .addr(counter_1_q), .we(Push), .clk(Clock), .din(counter_2_q), .dout(ram_1_dout), .clr(Reset));  // open: oe
  or or_2 (or_2_out, Pop, Set);
  Counter #(.max('hffff), .width(16)) counter_2 (
    .load(or_2_out), .D(multiplexer_2_out), .count(Enable), .Q(counter_2_q), .clk(Clock), .clr(Reset));  // open: carry, up
  assign Addr_Out = Enable ? counter_2_q : 16'bz;  // Controlled_Buffer controlled_buffer_1

  // Notes on the sheet:
  //   BIOS PAS COMPRIS DANS SYS
endmodule
